# Fritzing sketch ugame-10 (saved by Fritzing 0.9.3b)
circuit board: 4.19999cm x 4.99999cm
breadboards: 1

parts:
  X5 = SWITCH-MOMENTARY-2 [package=tactile-switch-1101ne]
  X6 = SWITCH-MOMENTARY-2 [package=tactile-switch-1101ne]
  X7 = SWITCH-MOMENTARY-2 [package=tactile-switch-1101ne]
  X4 = SWITCH-MOMENTARY-2 [package=tactile-switch-1101ne]
  X9 = SWITCH-MOMENTARY-2 [package=tactile-switch-1101ne]
  X8 = SWITCH-MOMENTARY-2 [package=tactile-switch-1101ne]
  X1 = USB Connectors [package=usb-microb]
  U1 = AT25FS010 [package=so08wide]
  C1 = Ceramic Capacitor [capacitance=1µF package="0603 [SMD, multilayer]"]
  U4 = Voltage Regulator LDO [package=sot23-5]
  C2 = Ceramic Capacitor [capacitance=1µF package="0603 [SMD, multilayer]"]
  D1 = Rectifier Diode [package="Melf DO-213 AA [SMD]"]
  U2 = mcp73831t
  R1 = Resistor [tolerance=±5% resistance=10k package="0402 [SMD]"]
  R2 = Resistor [tolerance=±5% resistance=2k package="0402 [SMD]"]
  R3 = Resistor [tolerance=±5% resistance=2.4k package="0402 [SMD]"]
  CHARGE = smd LED [color="Orange (605nm)" package="0603 [SMD]"]
  R4 = Resistor [tolerance=±5% resistance=300 package="0402 [SMD]"]
  X2 = SPST Switch [package=switch-spst-smd-a]
  Pad5 = Pad [width=7 height=2 connect=center]
  R6 = Resistor [tolerance=±5% resistance=47k package="0402 [SMD]"]
  R8 = Resistor [tolerance=±10% resistance=10k package="0402 [SMD]"]
  R7 = Resistor [tolerance=±10% resistance=47k package="0402 [SMD]"]
  C3 = Ceramic Capacitor [capacitance=100nF package="0603 [SMD, multilayer]"]
  SPKR = Pad [width=1.27 height=2.54 connect=center]
  + = Pad [width=1.27 height=2.54 connect=center]
  +_2 = Pad [width=2.6000000000000001 height=3 connect=center]
  SWCLK = Pad [width=2.54 height=2.54 connect=center]
  SWDIO = Pad [width=2.54 height=2.54 connect=center]
  - = Pad [width=2.6000000000000001 height=3 connect=center]
  R5 = Resistor [tolerance=±5% resistance=47k package="0402 [SMD]"]
  RESET = Pad [width=1.27 height=2.54 connect=center]
  X3 = Pad [width=1.27 height=2.54 connect=center]
  GND = Pad [width=2.54 height=2.54 connect=center]
  J1 = female pin header, 4 pins [form="♀ (female)"]
  +_- = female pin header, 2 pins [form="♀ (female)"]
  3V3 = Pad [width=2.54 height=2.54 connect=center]
  nRST = Pad [width=2.54 height=2.54 connect=center]
  U5 = PAM8301 [part_number=PAM8301AAF]
  U6 = st7735-14pin [part_number=ST7735]
  U3 = samd21e [chip_label=IC]

nets:
  GND: X5.1, X6.2, X7.2, X4.1, X9.2, X8.1, X1.GND, U1.GND, C1.0, U4.GND, C2.0, U2.connector1, R2.Pin_1, Pad5.pad, R6.Pin_0, -.pad, X3.pad, GND.pad, +_-.pin1, U5.connector4, U6.connector1, U6.connector2, U6.connector4, U6.connector12, U3.connector9, U3.connector27
  BUTTON UP: X5.2, U3.connector3
  BUTTON DOWN: X6.1, U3.connector20
  BUTTON RIGHT: X7.1, U3.connector5
  BUTTON LEFT: X4.2, U3.connector4
  BUTTON X: X9.1, U3.connector1
  BUTTON O: X8.2, U3.connector0
  USB D+: X1.D+, U3.connector23
  USB D-: X1.D-, U3.connector22
  N1: X1.VBUS, U4.IN, U4.EN, D1.cathode, U2.connector3, CHARGE.anode
  FLASH CS: U1.CS, R1.Pin_0, U3.connector18
  FLASH MISO: U1.SO, U3.connector19
  3.3V: U1.WP, U1.HOLD, U1.VCC, U4.OUT, C2.1, R1.Pin_1, R4.Pin_0, R8.Pin_1, 3V3.pad, U5.connector1, U6.connector9, U6.connector10, U3.connector8, U3.connector29
  FLASH MOSI: U1.SI, U3.connector16
  FLASH SCK: U1.SCK, U3.connector17
  N2: C1.1, U3.connector28
  N3: D1.anode, U2.connector2, X2.O, X2.P, R5.Pin_1
  N4: U2.connector0, R3.Pin_1
  N5: U2.connector4, R2.Pin_0
  N6: R3.Pin_0, CHARGE.cathode
  N7: R4.Pin_1, U6.connector3
  N8: X2.S, +_2.pad, +_-.pin2
  BATTERY: R6.Pin_1, R5.Pin_0, U3.connector12
  MUTE: R8.Pin_0, U5.connector2, U3.connector21
  N9: R7.Pin_0, C3.0
  SPEAKER: R7.Pin_1, U3.connector2
  N10: C3.1, U5.connector3
  N11: SPKR.pad, U5.connector5
  N12: +.pad, U5.connector0
  SWDCLK: SWCLK.pad, U3.connector30
  SWDIO: SWDIO.pad, U3.connector31
  RESET: RESET.pad, nRST.pad, U6.connector5, U3.connector25
  D: J1.pin1, U3.connector26
  C: J1.pin2, U3.connector15
  B: J1.pin3, U3.connector14
  A: J1.pin4, U3.connector13
  DISPLAY D/C: U6.connector6, U3.connector11
  DISPLAY MOSI: U6.connector7, U3.connector6
  DISPLAY SCK: U6.connector8, U3.connector7
  DISPLAY CS: U6.connector11, U3.connector10

notes:
  http://hackaday.io/project/27629
  A B C D
  o
  x
  .
  µGame, A python handheld game console., 10
